# Fritzing sketch hc05-D1mini (saved by Fritzing 0.9.3b)

parts:
  WeMos_D1_Mini = WeMos D1 Mini
  HC-05 = Bluetooth HC-05 (ZS-040) Male

nets:
  5V: WeMos_D1_Mini.5V, HC-05.VCC
  N1: WeMos_D1_Mini.D0, HC-05.EN
  N2: WeMos_D1_Mini.D5, HC-05.TXD
  N3: WeMos_D1_Mini.D6, HC-05.RXD
  N4: WeMos_D1_Mini.D7, HC-05.STATE
  N5: WeMos_D1_Mini.G, HC-05.GND

custom parts:
  Bluetooth HC-05 (ZS-040) Male: The zs-040 breakout boards are being used for many HC-05 Bluetooth modules. They also an EN pin rather than a KEY pin and they have a small button switch just above the EN pin.
