# Fritzing sketch hc05-Nano (saved by Fritzing 0.9.3b)
breadboards: 1

parts:
  R1 = Resistor [tolerance=±5% resistance=1k package=THT]
  R2 = Resistor [tolerance=±5% resistance=2k package=THT]
  part = Bluetooth HC-05 (ZS-040) Male
  part_2 = Arduino Nano (Rev3.0)

nets:
  N1: R1.Pin_0, part_2.D4
  N2: R1.Pin_1, R2.Pin_0, part.RXD
  GND: R2.Pin_1, part.GND, part_2.GND
  N3: part.STATE, part_2.D5
  N4: part.TXD, part_2.D3
  VCC: part.VCC, part_2.5V

custom parts:
  Bluetooth HC-05 (ZS-040) Male: The zs-040 breakout boards are being used for many HC-05 Bluetooth modules. They also an EN pin rather than a KEY pin and they have a small button switch just above the EN pin.
